# Fritzing sketch GO_CORONA_BOT (saved by Fritzing 0.9.3b)
breadboards: 1

parts:
  U1 = ESP32S-HiLetgo [part_number=ESP32S-HiLetgo]
  Grove1 = Grove OLED 128x96
  PIR1 = PIR sensor
  T1 = LM35 Temperature Sensor [package="TO92 [THT]"]
  Part1 = u-blox NEO-6M GPS Breakout
  J1 = Piezo Speaker
  LED1 = smd LED [color="Red (633nm)" package="0603 [SMD]"]
  R1 = Resistor [tolerance=±5% resistance=220 package="1206 [SMD]"]

nets:
  VCC: U1.3.3, Grove1.VCC, PIR1.VDD, T1.+Vs, Part1.VCC
  N1: U1.GPIO33, PIR1.SIG
  N2: U1.GPIO26, J1.pin2
  N3: U1.GPIO14, LED1.anode
  GND: U1.GND, Grove1.GND, PIR1.GND, T1.GND, Part1.GND, J1.pin1, R1.Pin_0
  N4: U1.GPIO4, T1.Vout
  N5: U1.GPIO16, Part1.TXD
  N6: U1.GPIO17, Part1.RXD
  N7: U1.GPIO21, Grove1.SDA
  N8: U1.GPIO22, Grove1.SCL
  N9: LED1.cathode, R1.Pin_1

custom parts:
  ESP32S-HiLetgo: HiLetgo ESP-WROOM-32 ESP32 ESP-32S Development Board 2.4GHz Dual-Mode WiFi + Bluetooth Dual Cores Microcontroller The ESP32 integrated with Antenna switches, RF Balun, power amplifiers, low-noise amplifiers, filters, and management modules, and the entire solution occupies the least area of PCB. 2.4 GHz Wi-Fi plus Bluetooth dual-mode chip, with TSMC Ultra-low power consumption 40nm technology,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
